// Logisim project RISC_V32_Proc.circ as structural Verilog: 6 circuits, main circuit Fetch
module RISCV32 (
);

  wire and_1_out, and_2_out, and_3_out, clock_1_out, decode_1_imm_active, decode_1_load, decode_1_lui,
       decode_1_mem_lui, decode_1_memory, decode_1_slt_active, decode_1_store, decode_1_word, nor_1_out,
       nor_2_out, not_1_out;
  wire [3:0] bit_extender_1_out, decode_1_opcode, decoder_1_out0, multiplexer_3_out;
  wire [4:0] registerfile_1_p3, registerfile_1_p4, registerfile_1_p5;
  wire [7:0] multiplexer_5_out;
  wire [19:0] execute_1_result_2;
  wire [31:0] bit_extender_2_out, decode_1_imm, execute_1_result, fetch_1_pc_out, multiplexer_1_out,
       multiplexer_2_out, multiplexer_4_out, ram_1_p7, registerfile_1_p1, registerfile_1_p6,
       registerfile_1_p7, risc_vprogramrom_1_p2;

  Clock clock_1 (.out(clock_1_out));
  Fetch fetch_1 (.Clk_In(clock_1_out), .PC_Out(fetch_1_pc_out));
  // RISC_VProgramROM risc_vprogramrom_1: pin names not known; wires that end beside it: fetch_1_pc_out, risc_vprogramrom_1_p2, clock_1_out
  and and_1 (and_1_out, ~nor_2_out, decode_1_load);  // AND_Gate
  nor nor_1 (nor_1_out, and_1_out, decode_1_store);
  // RegisterFile registerfile_1: pin names not known; wires that end beside it: registerfile_1_p1, nor_1_out, registerfile_1_p3, registerfile_1_p4, registerfile_1_p5, registerfile_1_p6, registerfile_1_p7
  Decode decode_1 (
    .Insn_In(risc_vprogramrom_1_p2), .Reg_Write(registerfile_1_p3), .Rs1(registerfile_1_p4),
    .Rs2(registerfile_1_p5), .Imm_Active(decode_1_imm_active), .Load(decode_1_load), .Store(decode_1_store),
    .Memory(decode_1_memory), .Word(decode_1_word), .SLT_Active(decode_1_slt_active),
    .Opcode(decode_1_opcode), .Imm(decode_1_imm), .Mem_LUI(decode_1_mem_lui), .LUI(decode_1_lui));
  and and_2 (and_2_out, decode_1_store, ~decode_1_word);  // AND_Gate
  Execute execute_1 (
    .A(registerfile_1_p6), .B(registerfile_1_p7), .Imm(decode_1_imm), .Op(decode_1_opcode),
    .Imm_Act(decode_1_imm_active), .SLT_Act(decode_1_slt_active), .Mem_LUI(decode_1_mem_lui),
    .LUI(decode_1_lui), .Result({execute_1_result[31:22], execute_1_result_2, execute_1_result[1:0]}));
  Multiplexer #(.select(2), .width(32), .enable("false")) multiplexer_1 (
    .in0(registerfile_1_p7),
    .in1({registerfile_1_p7[31:16], registerfile_1_p7[7:0], registerfile_1_p7[15:8]}),
    .in2({registerfile_1_p7[31:24], registerfile_1_p7[7:0], registerfile_1_p7[23:8]}),
    .in3({registerfile_1_p7[7:0], registerfile_1_p7[31:8]}), .out(multiplexer_1_out),
    .sel(execute_1_result[1:0]));
  Multiplexer #(.width(32), .enable("false")) multiplexer_2 (
    .in0(registerfile_1_p7), .in1(multiplexer_1_out), .out(multiplexer_2_out), .sel(and_2_out));
  Decoder #(.select(2), .enable("false")) decoder_1 (
    .out0(decoder_1_out0[0]), .out1(decoder_1_out0[1]), .out2(decoder_1_out0[2]), .out3(decoder_1_out0[3]),
    .sel(execute_1_result[1:0]));
  assign bit_extender_1_out = {{3{decode_1_word}}, decode_1_word};  // Bit_Extender bit_extender_1
  Multiplexer #(.width(4), .enable("false")) multiplexer_3 (
    .in0(decoder_1_out0), .in1(bit_extender_1_out), .out(multiplexer_3_out), .sel(decode_1_word));
  nor nor_2 (nor_2_out, execute_1_result[31], execute_1_result[30], execute_1_result[29], execute_1_result[28], execute_1_result[27], execute_1_result[26], execute_1_result[25], execute_1_result[24], execute_1_result[23], execute_1_result[22]);
  and and_3 (and_3_out, nor_2_out, decode_1_store);
  // RAM ram_1: pin names not known; wires that end beside it: execute_1_result_2, multiplexer_2_out, and_3_out, multiplexer_3_out, clock_1_out, decode_1_load, ram_1_p7
  Multiplexer #(.width(32), .enable("false")) multiplexer_4 (
    .in0(ram_1_p7), .in1(bit_extender_2_out), .out(multiplexer_4_out), .sel(not_1_out));
  assign bit_extender_2_out = {{24{multiplexer_5_out[7]}}, multiplexer_5_out};  // Bit_Extender bit_extender_2
  not not_1 (not_1_out, decode_1_word);
  Multiplexer #(.select(2), .width(8), .enable("false")) multiplexer_5 (
    .in0(ram_1_p7[7:0]), .in1(ram_1_p7[15:8]), .in2(ram_1_p7[23:16]), .in3(ram_1_p7[31:24]),
    .out(multiplexer_5_out), .sel(execute_1_result[1:0]));
  Multiplexer #(.width(32), .enable("false")) multiplexer_6 (
    .in0({execute_1_result[31:22], execute_1_result_2, execute_1_result[1:0]}), .in1(multiplexer_4_out),
    .out(registerfile_1_p1), .sel(decode_1_memory));

  // Notes on the sheet:
  //   Emulates the RISC-V 32-bit processor
  //   contents of risc_vprogramrom_1 (hex, n*v repeats v):
  //   #ALU that was provided was assumed to be operating correctly, test cases are focused on ensuring
  //   that the circuit #works with all the different functions. When coming to the random cases, each
  //   function is tested three times. #Specific Cases (Edge cases with memory and single test with all
  //   other functions) lui x1, 0xf0000                              #Testing excess memory address (store)
  //   and LUI and ADDI addi x2, x0, 0xf sw x2, 0(x1)  sw x2, 0(x0)                             #Testing
  //   excess memory address (load) lw x3, 0(x1)        addi x4, x0, 0xfff                    #Store byte
  //   with more than byte with value sb x4, 4(x0)  addi x5, x0, 0xef sb x5, 8(x0)
  //   #Store byte (1st byte)  sb x5, 9(x0)                            #Store byte (2nd byte)  sb x5,
  //   10(x0)                           #Store byte (3rd byte)  sb x5, 11(x0)
  //   #Store byte (4th byte)  lb x6, 8(x0)                            #Load byte (1st byte)  lb x7, 9(x0)
  //   #Load byte (2nd byte)  lb x8, 10(x0)                            #Load byte (3rd byte)  lb x9, 11(x0)
  //   #Load byte (4th byte)  add x10, x9, x8  sub x11, x9, x4  and x12, x8, x9  or x13, x11, x4  xor x14,
  //   x9, x4  slt x15, x5, x4  addi x16, x0, 8 sll x17, x5, x16  sra x18, x1, x16  andi x19, x4, 0xfff
  //   ori x20, x5, 0x80  xori x21, x4, 0xabc  slti x22, x5, 0xff                         #Random
  //   cases(each operation tested at least three times each)  add x23, x22, x21 add x24, x5, x4 add x25,
  //   x20, x17 sub x26, x19, x18 sub x27, x22, x20 sub x28, x4, x5 and x29, x21, x20 and x30, x15, x18 and
  //   x31, x18, x19  #clear registers add x1, x0, x0 add x2, x0, x0 add x3, x0, x0 add x4, x0, x0 add x5,
  //   x0, x0 add x6, x0, x0 add x7, x0, x0 add x8, x0, x0 add x9, x0, x0 add x10, x0, x0 add x11, x0, x0
  //   add x12, x0, x0 add x13, x0, x0 add x14, x0, x0 add x15, x0, x0 add x16, x0, x0 add x17, x0, x0 add
  //   x18, x0, x0 add x19, x0, x0 add x20, x0, x0 add x21, x0, x0 add x22, x0, x0 add x23, x0, x0 add x24,
  //   x0, x0 add x25, x0, x0 add x26, x0, x0 add x27, x0, x0 add x28, x0, x0 add x29, x0, x0 add x30, x0,
  //   x0 add x31, x0, x0   addi x1, x0, 0xfef addi x2, x0, 0x846 addi x3, x0, 0x4c4 lui x4, 0xadde7 or x5,
  //   x1, x2 or x6, x2, x3 or x7, x4, x3 xor x8, x7, x5   xor x9, x5, x6 xor x10, x4, x8 slt x11, x1, x2
  //   slt x12, x3, x4 slt x13, x6, x7 addi x14, x0, 9 addi x15, x0, 19 sll x16, x10, x14 sll x17, x7, x14
  //   sll x18, x11, x15 sra x19, x4, x14 sra x20, x4, x15 sra x21, x1, x14 andi x22, x20, 0x4ff andi x23,
  //   x7, 0x989 andi x24, x15, 0xfff ori x25, x12, 0x419 ori x26, x3, 0xff4 ori x27, x4, 0xce6 xori x28,
  //   x25, 0xfff xori x29, x15, 0x52a xori x30, x2, 0xad2  #clear registers add x1, x0, x0 add x2, x0, x0
  //   add x3, x0, x0 add x4, x0, x0 add x5, x0, x0 add x6, x0, x0 add x7, x0, x0 add x8, x0, x0 add x9,
  //   x0, x0 add x10, x0, x0 add x11, x0, x0 add x12, x0, x0 add x13, x0, x0 add x14, x0, x0 add x15, x0,
  //   x0 add x16, x0, x0 add x17, x0, x0 add x18, x0, x0 add x19, x0, x0 add x20, x0, x0 add x21, x0, x0
  //   add x22, x0, x0 add x23, x0, x0 add x24, x0, x0 add x25, x0, x0 add x26, x0, x0 add x27, x0, x0 add
  //   x28, x0, x0 add x29, x0, x0 add x30, x0, x0 add x31, x0, x0  addi x1, x0, 0xeff addi x2, x0, 0x481
  //   slti x3, x1, 0x001 slti x4, x2, 0x001 slti x5, x2, 0xfff lui x6, 0x4691a lui x7, 0xfedca sb x1,
  //   0(x0) sb x2, 1(x0) sb x4, 2(x0) sw x6, 4(x0) sw x7, 8(x0) sw x1, 12(x0) lb x8, 0(x0) lb x9, 1(x0) lb
  //   x10, 2(x0) lw x11, 4(x0) lw x12, 8(x0) lw x13, 12(x0)
endmodule

module Fetch (
  input  Clk_In,
  output [31:0] PC_Out
);

  wire [29:0] incrementer_1_p2;

  // Incrementer #(.width(30)) incrementer_1: pin names not known; wires that end beside it: PC_Out[31:2], incrementer_1_p2
  Register #(.width(32)) register_1 (
    .D({incrementer_1_p2, PC_Out[1:0]}), .en(Clk_In), .clk(Clk_In), .Q(PC_Out));  // open: clr

  // Notes on the sheet:
  //   Calculates and updates PC value
endmodule

module Decode (
  input  [31:0] Insn_In,
  output [4:0] Reg_Write,
  output [4:0] Rs1,
  output [4:0] Rs2,
  output Imm_Active,
  output Load,
  output Store,
  output Memory,
  output Word,
  output SLT_Active,
  output [3:0] Opcode,
  output [31:0] Imm,
  output Mem_LUI,
  output LUI
);

  wire and_1_out, and_2_out, and_3_out, and_6_out, and_7_out, not_1_out;
  wire [11:0] bit_extender_2_out, multiplexer_1_out;
  wire [31:0] bit_extender_1_out;

  and and_1 (and_1_out, ~Insn_In[6], Insn_In[5], Insn_In[4], ~Insn_In[3], ~Insn_In[2], Insn_In[1], Insn_In[0]);  // AND_Gate
  and and_2 (and_2_out, ~Insn_In[6], ~Insn_In[5], Insn_In[4], ~Insn_In[3], ~Insn_In[2], Insn_In[1], Insn_In[0]);  // AND_Gate
  Multiplexer #(.width(12), .enable("false")) multiplexer_1 (
    .in0(Insn_In[31:20]), .in1({Insn_In[31:25], Insn_In[11:7]}), .out(multiplexer_1_out), .sel(Store));
  not not_1 (not_1_out, LUI);
  and and_3 (and_3_out, ~Insn_In[31], ~Insn_In[30], ~Insn_In[29], ~Insn_In[28], ~Insn_In[27], ~Insn_In[26], ~Insn_In[25]);  // AND_Gate
  and and_4 (Word, ~Insn_In[14], Insn_In[13], ~Insn_In[12]);  // AND_Gate
  Opcode_Gen opcode_gen_1 (.Funct3(Insn_In[14:12]), .Funct7(Insn_In[31:25]), .Opcode(Insn_In[6:0]), .ALU_Op(Opcode));
  assign bit_extender_1_out = {{20{multiplexer_1_out[11]}}, multiplexer_1_out};  // Bit_Extender bit_extender_1
  assign bit_extender_2_out = {{11{1'b0}}, not_1_out};  // Bit_Extender bit_extender_2
  and and_5 (LUI, ~Insn_In[6], Insn_In[5], Insn_In[4], ~Insn_In[3], Insn_In[2], Insn_In[1], Insn_In[0]);  // AND_Gate
  and and_6 (and_6_out, and_3_out, and_1_out, Word);
  and and_7 (and_7_out, Word, and_2_out);
  Multiplexer #(.width(32), .enable("false")) multiplexer_2 (
    .in0(bit_extender_1_out), .in1({Insn_In[31:12], bit_extender_2_out}), .out(Imm), .sel(LUI));
  and and_8 (Load, ~Insn_In[6], ~Insn_In[5], ~Insn_In[4], ~Insn_In[3], ~Insn_In[2], Insn_In[1], Insn_In[0]);  // AND_Gate
  and and_9 (Store, ~Insn_In[6], Insn_In[5], ~Insn_In[4], ~Insn_In[3], ~Insn_In[2], Insn_In[1], Insn_In[0]);  // AND_Gate
  or or_1 (Memory, Store, Load);
  or or_2 (SLT_Active, and_6_out, and_7_out);
  nand nand_1 (Imm_Active, ~Insn_In[6], Insn_In[5], Insn_In[4], ~Insn_In[3], ~Insn_In[2], Insn_In[1], Insn_In[0]);  // NAND_Gate
  or or_3 (Mem_LUI, Memory, LUI);

  assign Reg_Write = Insn_In[11:7];
  assign Rs1 = Insn_In[19:15];
  assign Rs2 = Insn_In[24:20];

  // Notes on the sheet:
  //   Breaks down instruction for use in the other parts of the processor
endmodule

module Execute (
  input  [31:0] A,
  input  [31:0] B,
  input  [31:0] Imm,
  input  [3:0] Op,
  input  Imm_Act,
  input  SLT_Act,
  input  Mem_LUI,
  input  LUI,
  output [31:0] Result
);

  wire comparator_black_box_1_p4, not_1_out;
  wire [3:0] alu_1_p3;
  wire [3:2] not_3_out;
  wire [31:0] alu_1_p5, bit_extender_1_out, bit_extender_2_out, multiplexer_1_out, multiplexer_2_out,
       multiplexer_3_out;

  Multiplexer #(.width(32), .enable("false")) multiplexer_1 (
    .in0(B), .in1(Imm), .out(multiplexer_1_out), .sel(Imm_Act));
  assign bit_extender_1_out = {{31{1'b0}}, not_1_out};  // Bit_Extender bit_extender_1
  not not_1 (not_1_out, LUI);
  not not_2 (not_3_out[3], Mem_LUI);
  not not_3 (not_3_out[2], Mem_LUI);
  // Comparator_Black_Box comparator_black_box_1: pin names not known; wires that end beside it: A, multiplexer_1_out, SLT_Act, comparator_black_box_1_p4
  Multiplexer #(.width(32), .enable("false")) multiplexer_2 (
    .in0(A), .in1(bit_extender_1_out), .out(multiplexer_2_out), .sel(LUI));
  Multiplexer #(.width(32), .enable("false")) multiplexer_3 (
    .in0(B), .in1(Imm), .out(multiplexer_3_out), .sel(Imm_Act));
  // ALU alu_1: pin names not known; wires that end beside it: multiplexer_2_out, multiplexer_3_out, alu_1_p3, multiplexer_3_out[4:0], alu_1_p5
  Multiplexer #(.width(4), .enable("false")) multiplexer_4 (
    .in0(Op), .in1({not_3_out, {2{Mem_LUI}}}), .out(alu_1_p3), .sel(Mem_LUI));
  assign bit_extender_2_out = {{31{1'b0}}, comparator_black_box_1_p4};  // Bit_Extender bit_extender_2
  Multiplexer #(.width(32), .enable("false")) multiplexer_5 (
    .in0(alu_1_p5), .in1(bit_extender_2_out), .out(Result), .sel(SLT_Act));

  // Notes on the sheet:
  //   Calculates the ALU operation and SLT(I) operation
endmodule

module Opcode_Gen (
  input  [2:0] Funct3,
  input  [6:0] Funct7,
  input  [6:0] Opcode,
  output [3:0] ALU_Op
);

  wire funct_check_1_sll_active;
  wire [3:0] and_1_out, and_2_out, and_3_out, and_4_out, and_5_out, and_6_out, and_7_out, bit_extender_1_out,
       bit_extender_2_out, bit_extender_3_out, bit_extender_4_out, bit_extender_5_out, bit_extender_6_out,
       bit_extender_7_out, not_3_out, not_9_out, not_11_out, not_14_out, not_17_out;
  wire [3:1] not_5_out, not_12_out;

  Funct_Check funct_check_1 (
    .Funct_3(Funct3), .Funct_7(Funct7), .Opcode(Opcode), .AND_Active(not_3_out[2]), .OR_Active(not_5_out[2]),
    .SLL_Active(funct_check_1_sll_active), .XOR_Active(not_11_out[3]), .SRA_Active(not_12_out[3]),
    .SUB_Active(not_14_out[2]), .ADD_Active(not_17_out[1]));
  not not_1 (not_3_out[3], not_3_out[2]);
  not not_2 (not_3_out[1], not_3_out[2]);
  not not_3 (not_3_out[0], not_3_out[2]);
  not not_4 (not_5_out[3], not_5_out[2]);
  not not_5 (not_5_out[1], not_5_out[2]);
  not not_6 (not_9_out[3], funct_check_1_sll_active);
  not not_7 (not_9_out[2], funct_check_1_sll_active);
  not not_8 (not_9_out[1], funct_check_1_sll_active);
  not not_9 (not_9_out[0], funct_check_1_sll_active);
  not not_10 (not_11_out[2], not_11_out[3]);
  not not_11 (not_11_out[0], not_11_out[3]);
  not not_12 (not_12_out[1], not_12_out[3]);
  not not_13 (not_14_out[3], not_14_out[2]);
  not not_14 (not_14_out[0], not_14_out[2]);
  not not_15 (not_17_out[3], not_17_out[1]);
  not not_16 (not_17_out[2], not_17_out[1]);
  not not_17 (not_17_out[0], not_17_out[1]);
  assign bit_extender_1_out = {{3{not_17_out[1]}}, not_17_out[1]};  // Bit_Extender bit_extender_1
  assign bit_extender_2_out = {{3{not_3_out[2]}}, not_3_out[2]};  // Bit_Extender bit_extender_2
  assign bit_extender_3_out = {{3{not_5_out[2]}}, not_5_out[2]};  // Bit_Extender bit_extender_3
  assign bit_extender_4_out = {{3{funct_check_1_sll_active}}, funct_check_1_sll_active};  // Bit_Extender bit_extender_4
  assign bit_extender_5_out = {{3{not_11_out[3]}}, not_11_out[3]};  // Bit_Extender bit_extender_5
  assign bit_extender_6_out = {{3{not_12_out[3]}}, not_12_out[3]};  // Bit_Extender bit_extender_6
  assign bit_extender_7_out = {{3{not_14_out[2]}}, not_14_out[2]};  // Bit_Extender bit_extender_7
  assign and_1_out = bit_extender_2_out & not_3_out;  // AND_Gate and_1, 4 bits wide
  assign and_2_out = bit_extender_3_out & {not_5_out, not_5_out[2]};  // AND_Gate and_2, 4 bits wide
  assign and_3_out = bit_extender_4_out & not_9_out;  // AND_Gate and_3, 4 bits wide
  assign and_4_out = bit_extender_5_out & {not_11_out[3:2], not_11_out[3], not_11_out[0]};  // AND_Gate and_4, 4 bits wide
  assign and_5_out = bit_extender_6_out & {{2{not_12_out[3]}}, not_12_out[1], not_12_out[3]};  // AND_Gate and_5, 4 bits wide
  assign and_6_out = bit_extender_7_out & {not_14_out[3:2], not_14_out[2], not_14_out[0]};  // AND_Gate and_6, 4 bits wide
  assign and_7_out = bit_extender_1_out & not_17_out;  // AND_Gate and_7, 4 bits wide
  assign ALU_Op = and_1_out | and_2_out | and_3_out | and_4_out | and_5_out | and_6_out | and_7_out;  // OR_Gate or_1, 4 bits wide

  // Notes on the sheet:
  //   Generates the opcode for the ALU
  //   0100
  //   0101
  //   0000
  //   1010
  //   1101
  //   0110
  //   0010
endmodule

module Funct_Check (
  input  [2:0] Funct_3,
  input  [6:0] Funct_7,
  input  [6:0] Opcode,
  output AND_Active,
  output OR_Active,
  output SLL_Active,
  output XOR_Active,
  output SRA_Active,
  output SUB_Active,
  output ADD_Active
);

  wire and_1_out, and_2_out, and_3_out, and_4_out, and_5_out, and_6_out, and_7_out, and_8_out, and_9_out,
       and_10_out, and_11_out, and_12_out, and_13_out, and_14_out, and_15_out, and_16_out, and_17_out,
       and_18_out, and_19_out, and_20_out, and_21_out, and_22_out, I_out, R_out;

  and R (R_out, ~Opcode[6], Opcode[5], Opcode[4], ~Opcode[3], ~Opcode[2], Opcode[1], Opcode[0]);  // AND_Gate
  and I (I_out, ~Opcode[6], ~Opcode[5], Opcode[4], ~Opcode[3], ~Opcode[2], Opcode[1], Opcode[0]);  // AND_Gate
  and and_1 (and_1_out, ~Funct_7[6], ~Funct_7[5], ~Funct_7[4], ~Funct_7[3], ~Funct_7[2], ~Funct_7[1], ~Funct_7[0]);  // AND_Gate
  and and_2 (and_2_out, ~Funct_7[6], ~Funct_7[5], ~Funct_7[4], ~Funct_7[3], ~Funct_7[2], ~Funct_7[1], ~Funct_7[0]);  // AND_Gate
  and and_3 (and_3_out, ~Funct_7[6], ~Funct_7[5], ~Funct_7[4], ~Funct_7[3], ~Funct_7[2], ~Funct_7[1], ~Funct_7[0]);  // AND_Gate
  and and_4 (and_4_out, ~Funct_3[2], ~Funct_3[1], ~Funct_3[0]);  // AND_Gate
  and and_5 (and_5_out, Funct_3[2], Funct_3[1], Funct_3[0]);
  and and_6 (and_6_out, ~Funct_7[6], ~Funct_7[5], ~Funct_7[4], ~Funct_7[3], ~Funct_7[2], ~Funct_7[1], ~Funct_7[0]);  // AND_Gate
  and and_7 (and_7_out, Funct_3[2], Funct_3[1], ~Funct_3[0]);  // AND_Gate
  and and_8 (and_8_out, Funct_3[2], ~Funct_3[1], ~Funct_3[0]);  // AND_Gate
  and and_9 (and_9_out, R_out, and_3_out, and_4_out);
  and and_10 (and_10_out, and_1_out, R_out, and_5_out);
  and and_11 (and_11_out, and_5_out, I_out);
  and and_12 (and_12_out, and_6_out, R_out, and_7_out);
  and and_13 (and_13_out, and_7_out, I_out);
  and and_14 (and_14_out, ~Funct_7[6], ~Funct_7[5], ~Funct_7[4], ~Funct_7[3], ~Funct_7[2], ~Funct_7[1], ~Funct_7[0]);  // AND_Gate
  and and_15 (and_15_out, ~Funct_3[2], ~Funct_3[1], Funct_3[0]);  // AND_Gate
  and and_16 (and_16_out, and_2_out, R_out, and_8_out);
  and and_17 (and_17_out, and_8_out, I_out);
  and and_18 (and_18_out, Funct_3[2], ~Funct_3[1], Funct_3[0]);  // AND_Gate
  and and_19 (and_19_out, ~Funct_7[6], Funct_7[5], ~Funct_7[4], ~Funct_7[3], ~Funct_7[2], ~Funct_7[1], ~Funct_7[0]);  // AND_Gate
  and and_20 (and_20_out, ~Funct_3[2], ~Funct_3[1], ~Funct_3[0]);  // AND_Gate
  and and_21 (and_21_out, ~Funct_7[6], Funct_7[5], ~Funct_7[4], ~Funct_7[3], ~Funct_7[2], ~Funct_7[1], ~Funct_7[0]);  // AND_Gate
  and and_22 (and_22_out, and_4_out, I_out);
  or or_1 (AND_Active, and_10_out, and_11_out);
  or or_2 (OR_Active, and_12_out, and_13_out);
  and and_23 (SLL_Active, and_14_out, R_out, and_15_out);
  or or_3 (XOR_Active, and_16_out, and_17_out);
  and and_24 (SRA_Active, and_18_out, R_out, and_19_out);
  and and_25 (SUB_Active, and_20_out, R_out, and_21_out);
  or or_4 (ADD_Active, and_9_out, and_22_out);

  // Notes on the sheet:
  //   Checks which function may be called
endmodule
